# Fritzing sketch WaterFlowSensorESP32 (saved by Fritzing 0.9.6b)

parts:
  YF-S201_Flow_Meter1 = YF-S201 Water Flow Meter
  Mod1 = Heltec WiFi LoRa 32 V2 [part_number=HTIT-WB32LA]

nets:
  N1: YF-S201_Flow_Meter1.SIG, Mod1.pin_15
  GND: YF-S201_Flow_Meter1.GND, Mod1.GND
  N2: YF-S201_Flow_Meter1.VCC, Mod1.pin_20

custom parts:
  YF-S201 Water Flow Meter: The YF-S201 Flow Meter. The input voltage is 5V to 24V (DC).
